# Fritzing sketch Garden_Pi_Fritzing (saved by Fritzing 0.9.10b)
breadboards: 1

parts:
  High_H2O_Soil_Humidity_Sensor = Adafruit STEMMA Soil Sensor - I2C Capacitive Moisture Sensor [part_number="Adafruit #4026"]
  Mod1 = Raspberry Pi 4B
  Low_H2O_Soil_Humidity_Sensor = Adafruit STEMMA Soil Sensor - I2C Capacitive Moisture Sensor [part_number="Adafruit #4026"]
  Potted_Plant_Humidity_Sensor = Adafruit STEMMA Soil Sensor - I2C Capacitive Moisture Sensor [part_number="Adafruit #4026"]
  Valve3_(Pot_H2O) = DC Motor [voltage_(max)=12V voltage_(min)=3V]
  Valve2_(Low_H2O) = DC Motor [voltage_(max)=12V voltage_(min)=3V]
  Garden_Camera_(Ribbon_Cable) = Rasberry Pi NIOR Camera [chip_label=IC package="DIP (Dual Inline) [THT]"]  # not connected
  U1 = 4-Channel 5v Relay Shield [package=relay-4ch5v10a]
  12V_Power = 2.1mm Barrel Jack with Terminal Block
  5V_Power_(Board) = 2.1mm Barrel Jack with Terminal Block
  Valve1_(High_H2O) = DC Motor [voltage_(max)=12V voltage_(min)=3V]

nets:
  GND: High_H2O_Soil_Humidity_Sensor.GND, Low_H2O_Soil_Humidity_Sensor.GND, Potted_Plant_Humidity_Sensor.GND, U1.GND, 5V_Power_(Board).NEG
  VIN: High_H2O_Soil_Humidity_Sensor.VIN, Low_H2O_Soil_Humidity_Sensor.VIN, Potted_Plant_Humidity_Sensor.VIN, U1.VCC, 5V_Power_(Board).POS
  3V3: High_H2O_Soil_Humidity_Sensor.SDA, Mod1.3V3, Mod1.5V, Mod1.GPIO2, Mod1.GPIO24, Low_H2O_Soil_Humidity_Sensor.SDA, Potted_Plant_Humidity_Sensor.SDA
  N1: High_H2O_Soil_Humidity_Sensor.SCL, Mod1.GPIO3, Mod1.GND, Mod1.GPIO15, Mod1.GPIO27, Mod1.GPIO10, Mod1.GPIO7, Mod1.GPIO5, Mod1.GPIO13, Mod1.GPIO21, Low_H2O_Soil_Humidity_Sensor.SCL, Potted_Plant_Humidity_Sensor.SCL, U1.IN3
  N2: Mod1.GPIO4, Mod1.GPIO14, U1.IN2
  N3: Mod1.GPIO17, Mod1.GPIO18, U1.IN4
  N4: Mod1.GPIO22, Mod1.GPIO23
  N5: Mod1.GPIO9, Mod1.GPIO25
  N6: Mod1.GPIO11, Mod1.GPIO8
  N7: Mod1.ID_SD, Mod1.ID_SC
  N8: Mod1.GPIO6, Mod1.GPIO12
  N9: Mod1.GPIO19, Mod1.GPIO16
  N10: Mod1.GPIO26, Mod1.GPIO20
  N11: Valve3_(Pot_H2O).pin_1, U1.K4-On
  N12: Valve3_(Pot_H2O).pin_2, Valve2_(Low_H2O).pin_2, 12V_Power.NEG, Valve1_(High_H2O).pin_2
  N13: Valve2_(Low_H2O).pin_1, U1.K3-On
  N14: U1.K2-In, U1.K3-In, U1.K4-In, 12V_Power.POS
  N15: U1.K2-On, Valve1_(High_H2O).pin_1

custom parts:
  Adafruit STEMMA Soil Sensor - I2C Capacitive Moisture Sensor: Most low cost soil sensors are resistive style, where there's two prongs and the sensor measures the conductivity between the two. These work OK at first, but eventually start to oxidize because of the exposed metal. Even if they're gold plated! The resistivity measurement goes up and up, so you constantly have to re-calibrate your code. Also, resistive measurements don't always work in loose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
  Rasberry Pi NIOR Camera: Camera
  4-Channel 5v Relay Shield: 4 Channel 5v Relay Shield w. 2x SPD-06VDC-SD-C
